# Fritzing sketch totalCircuit (saved by Fritzing 0.8.7b)
breadboards: 1

parts:
  부품1 = Arduino Uno (Rev3) - ICSP
  BT1 = Bluetooth HC-06d [package=THT]
  U1 = prefix0000
  M1 = Stepper Motor - Unipolar
  BAT1 = Battery Holders [package=lipo-1100mAh]
  M2 = DC Motor
  BAT2 = Battery Holders [package=lipo-1100mAh]
  MD03A2 = Dual VNH2SP30 Motor Driver [part_number=MD03A]
  U2 = SWITCH_SPDT [package=kps-1290]
  U3 = SWITCH_SPDT [package=kps-1290]

nets:
  N1: 부품1.ICSP_MISO, 부품1.D12/MISO, MD03A2.2CS
  N2: 부품1.ICSP_MOSI, 부품1.D11_PWM/MOSI, MD03A2.2PWM
  N3: 부품1.D2, BT1.TXD
  N4: 부품1.D3_PWM, BT1.RXD
  N5: 부품1.D4, U1.connector9
  N6: 부품1.D5_PWM, U1.connector11
  5V: 부품1.5V, BT1.VCC, U1.connector7
  GND: 부품1.GND, BT1.GND, MD03A2.GND#138, U3.O
  N7: 부품1.VIN, BAT2.+
  N8: U1.connector0, M1.D
  N9: U1.connector1, M1.B
  N10: U1.connector2, M1.C
  N11: U1.connector3, M1.A
  N12: U1.connector4, BAT1.+, MD03A2.VIN
  N13: U1.connector5, U2.O
  N14: BAT1.-, MD03A2.GND#151, U2.P
  N15: M2.pin_1, MD03A2.OUT_2A
  N16: M2.pin_2, MD03A2.OUT_2B
  N17: BAT2.-, U3.P

custom parts:
  Bluetooth HC-06d: Bluetooth HC-06 - face down, pins down 16.5mm x 37.5mm PCB
