# Fritzing sketch AI_Car (saved by Fritzing 0.8.7b)

parts:
  부품1 = Arduino Mega ADK (Rev3)
  부품2 = Bluetooth HM-10

nets:
  N1: 부품1.D15/RX3, 부품2.TXD
  N2: 부품1.D14/TX3, 부품2.RXD
  5V: 부품1.5V, 부품2.VCC
  GND: 부품1.GND, 부품2.GND
